// Logisim project ID_to_MUX_7segment_LCD.circ as structural Verilog: 1 circuit, main circuit main
module main (
  input  A,
  input  B,
  input  C
);

  wire a_out, A_prime_B_prime_C_out, A_prime_B_prime_out, AB_out, AC_prime_out, b_out, B_prime_C_out,
       B_prime_C_prime_out, BC_2_out, BC_out, BC_prime_out, c_out, e_out, f_out, g_out, nor_1_out, nor_2_out,
       nor_3_out, nor_4_out, nor_5_out, nor_6_out, nor_7_out, nor_8_out, nor_9_out;

  nor nor_1 (nor_1_out, A, A);
  nor nor_2 (nor_2_out, B, B);
  nor nor_3 (nor_3_out, C, C);
  nor A_prime_B_prime (A_prime_B_prime_out, B, A);
  nor BC (BC_out, nor_2_out, nor_3_out);
  nor AC_prime (AC_prime_out, nor_1_out, C);
  nor BC_prime (BC_prime_out, nor_2_out, C);
  nor B_prime_C (B_prime_C_out, B, nor_3_out);
  nor AB (AB_out, nor_1_out, nor_2_out);
  nor BC_2 (BC_2_out, nor_2_out, nor_3_out);
  nor A_prime_B_prime_C (A_prime_B_prime_C_out, A, B, nor_3_out);
  nor B_prime_C_prime (B_prime_C_prime_out, B, C);
  nor nor_4 (nor_4_out, A_prime_B_prime_out, BC_out, AC_prime_out);
  nor nor_5 (nor_5_out, nor_1_out, B, C);
  nor nor_6 (nor_6_out, A, BC_prime_out, B_prime_C_out);
  nor nor_7 (nor_7_out, A_prime_B_prime_out, AB_out, BC_2_out);
  nor nor_8 (nor_8_out, AC_prime_out, A_prime_B_prime_C_out);
  nor nor_9 (nor_9_out, AB_out, BC_2_out, B_prime_C_prime_out);
  _7_Segment_Display u_7_segment_display_1 (
    .g(g_out), .f(f_out), .a(a_out), .b(b_out), .e(e_out), .d(a_out), .c(c_out));  // open: dp
  nor u_a (a_out, nor_4_out, nor_4_out);
  nor u_b (b_out, nor_5_out, nor_5_out);
  nor u_c (c_out, nor_6_out, nor_6_out);
  nor e (e_out, nor_7_out, nor_7_out);
  nor f (f_out, nor_8_out, nor_8_out);
  nor g (g_out, nor_9_out, nor_9_out);

  // Notes on the sheet:
  //   a=(A'B'+BC+AC')
  //   d=(A'B'+BC+AC')
  //   A'B'
  //   AC'
  //   AB
  //   BC
  //   b=A'+B+C
  //   e=(A'B'+AB+BC)
  //   g=(B'C'+BC+AB)
  //   (A'B'+BC+AC')'
  //   (A'+B+C)'
  //   (A+BC'+B'C)'
  //   (A'B'+AB+BC)'
  //   (A'B'C+AC')'
  //   (B'C'+BC+AB)'
  //   c=(A+BC'+B'C)
  //   f=(A'B'C+AC')
  //   d
endmodule
