// Logisim project Practice.circ as structural Verilog: 8 circuits, main circuit 3-extend w x y z Basic
module _3_extend_w_x_y_z_Basic (
  input  A,
  input  B,
  input  C,
  input  D
);

  wire nand7400_1__1y, nand7400_2__1y, nand7400_3__1y, nand7400_4__1y, nand7400_5__1y, nand7400_5__2y,
       nand7400_6__1y, nand7400_6__2y, nand7400_6__3y, nand7400_6__4y, nand7400_7__1y, nand7400_7__2y,
       nand7400_7__4y, nand7400_8__2y, nand7400_8__3y, nand7400_8__4y, nand7400_10__1y, nand7400_11__1y,
       nand7400_11__2y, nand7400_11__4y;

  NAND7400 nand7400_1 (._1A(A), ._1B(A), ._1Y(nand7400_1__1y));  // open: _2A, _2B, _2Y, _3A, _3B, _3Y, _4A, _4B, _4Y
  NAND7400 nand7400_2 (._1A(B), ._1B(B), ._1Y(nand7400_2__1y));  // open: _2A, _2B, _2Y, _3A, _3B, _3Y, _4A, _4B, _4Y
  NAND7400 nand7400_3 (._1A(C), ._1B(C), ._1Y(nand7400_3__1y));  // open: _2A, _2B, _2Y, _3A, _3B, _3Y, _4A, _4B, _4Y
  NAND7400 nand7400_4 (._1A(D), ._1B(D), ._1Y(nand7400_4__1y));  // open: _2A, _2B, _2Y, _3A, _3B, _3Y, _4A, _4B, _4Y
  NAND7400 nand7400_5 (
    ._1A(B), ._1B(nand7400_3__1y), ._1Y(nand7400_5__1y), ._2A(nand7400_5__1y), ._2B(nand7400_5__1y),
    ._2Y(nand7400_5__2y));  // open: _3A, _3B, _3Y, _4A, _4B, _4Y
  NAND7400 nand7400_6 (
    ._1A(B), ._1B(nand7400_3__1y), ._1Y(nand7400_6__1y), ._2A(nand7400_6__1y), ._2B(nand7400_6__1y),
    ._2Y(nand7400_6__2y), ._3A(nand7400_6__4y), ._3B(nand7400_6__4y), ._3Y(nand7400_6__3y),
    ._4A(nand7400_6__2y), ._4B(nand7400_4__1y), ._4Y(nand7400_6__4y));
  NAND7400 nand7400_7 (
    ._1A(nand7400_2__1y), ._1B(D), ._1Y(nand7400_7__1y), ._2A(nand7400_7__1y), ._2B(nand7400_7__1y),
    ._2Y(nand7400_7__2y), ._4A(nand7400_7__2y), ._4B(nand7400_7__2y), ._4Y(nand7400_7__4y));  // open: _3A, _3B, _3Y
  NAND7400 nand7400_8 (
    ._2A(B), ._2B(C), ._2Y(nand7400_8__2y), ._3A(nand7400_8__2y), ._3B(nand7400_8__2y), ._3Y(nand7400_8__3y),
    ._4A(nand7400_8__3y), ._4B(nand7400_1__1y), ._4Y(nand7400_8__4y));  // open: _1A, _1B, _1Y
  NAND7400 nand7400_9 ();  // open: _1A, _1B, _1Y, _2A, _2B, _2Y, _3A, _3B, _3Y, _4A, _4B, _4Y
  NAND7400 nand7400_10 (
    ._1A(nand7400_5__2y), ._1B(nand7400_5__2y), ._1Y(nand7400_10__1y));  // open: _2A, _2B, _2Y, _3A, _3B, _3Y, _4A, _4B, _4Y
  NAND7400 nand7400_11 (
    ._1A(nand7400_6__3y), ._1B(nand7400_10__1y), ._1Y(nand7400_11__1y), ._2A(nand7400_11__1y),
    ._2B(nand7400_7__4y), ._2Y(nand7400_11__2y), ._4A(nand7400_11__2y), ._4B(nand7400_11__2y),
    ._4Y(nand7400_11__4y));  // open: _3A, _3B, _3Y

  // Notes on the sheet:
  //   Md. Ishtiaq Ahamed Fahim 2012518642 
endmodule

// 7408 AND
module AND7408 (
  input  _1A,
  input  _3A,
  input  _1B,
  input  _3B,
  input  _2A,
  input  _4A,
  input  _2B,
  input  _4B,
  output _1Y,
  output _3Y,
  output _2Y,
  output Y4
);

  and and_1 (_1Y, _1A, _1B);
  and and_2 (_2Y, _2A, _2B);
  and and_3 (_3Y, _3A, _3B);
  and and_4 (Y4, _4A, _4B);
endmodule

// NAND
module NAND7400 (
  input  _1A,
  input  _3A,
  input  _1B,
  input  _3B,
  input  _2A,
  input  _4A,
  input  _2B,
  input  _4B,
  output _1Y,
  output _3Y,
  output _2Y,
  output _4Y
);

  wire and_1_out, and_2_out, and_3_out, and_4_out;

  and and_1 (and_1_out, _1A, _1B);
  and and_2 (and_2_out, _2A, _2B);
  not not_1 (_3Y, and_3_out);
  not not_2 (_1Y, and_1_out);
  not not_3 (_4Y, and_4_out);
  not not_4 (_2Y, and_2_out);
  and and_3 (and_3_out, _3A, _3B);
  and and_4 (and_4_out, _4A, _4B);
endmodule

// 7432 OR
module OR7432 (
  input  _1A,
  input  _3A,
  input  _1B,
  input  _3B,
  input  _2A,
  input  _4A,
  input  _2B,
  input  _4B,
  output _1Y,
  output _3Y,
  output _2Y,
  output _4Y
);

  or or_1 (_1Y, _1A, _1B);
  or or_2 (_2Y, _2A, _2B);
  or or_3 (_3Y, _3A, _3B);
  or or_4 (_4Y, _4A, _4B);
endmodule

// 7404 NOT
module NOT7404 (
  input  _1A,
  input  _4A,
  input  _2A,
  input  _5A,
  input  _3A,
  input  _6A,
  output _1Y,
  output _4Y,
  output _2Y,
  output _5Y,
  output _3Y,
  output _6Y
);

  not not_1 (_1Y, _1A);
  not not_2 (_2Y, _2A);
  not not_3 (_3Y, _3A);
  not not_4 (_4Y, _4A);
  not not_5 (_5Y, _5A);
  not not_6 (_6Y, _6A);
endmodule

module XOR7486 (
  input  _1A,
  input  _3A,
  input  _1B,
  input  _3B,
  input  _2A,
  input  _4A,
  input  _2B,
  input  _4B,
  output _1Y,
  output _3Y,
  output _2Y,
  output _4Y
);

  xor xor_1 (_1Y, _1A, _1B);
  xor xor_2 (_2Y, _2A, _2B);
  xor xor_3 (_3Y, _3A, _3B);
  xor xor_4 (_4Y, _4A, _4B);
endmodule

// 7402 NOR
module NOR7402 (
  input  _1A,
  input  _3A,
  input  _1B,
  input  _3B,
  input  _2A,
  input  _4A,
  input  _2B,
  input  _4B,
  output _1Y,
  output _3Y,
  output _2Y,
  output _4Y
);

  wire or_1_out, or_2_out, or_3_out, or_4_out;

  or or_1 (or_1_out, _1A, _1B);
  or or_2 (or_2_out, _2A, _2B);
  not not_1 (_3Y, or_3_out);
  not not_2 (_1Y, or_1_out);
  not not_3 (_2Y, or_2_out);
  not not_4 (_4Y, or_4_out);
  or or_3 (or_3_out, _3A, _3B);
  or or_4 (or_4_out, _4A, _4B);
endmodule

module _3_extend_w_x_y_z_NOR (
  input  A,
  input  B,
  input  C,
  input  D,
  input  A_2,
  input  B_2,
  input  C_2,
  input  D_2,
  input  A_3,
  input  B_3,
  input  C_3,
  input  D_3,
  input  A_4,
  input  B_4,
  input  C_4,
  input  D_4,
  output W,
  output X,
  output Y,
  output Z
);

  wire nor7402_1__1y, nor7402_1__2y, nor7402_1__3y, nor7402_1__4y, nor7402_2__1y, nor7402_2__2y,
       nor7402_2__3y, nor7402_2__4y, nor7402_4__1y, nor7402_5__1y, nor7402_5__2y, nor7402_5__3y,
       nor7402_5__4y, nor7402_7__1y, nor7402_7__2y, nor7402_7__3y, nor7402_7__4y, nor7402_8__1y,
       nor7402_8__2y, nor7402_8__3y;

  NOR7402 nor7402_1 (
    ._1A(B), ._1B(B), ._1Y(nor7402_1__1y), ._2A(C), ._2B(C), ._2Y(nor7402_1__2y), ._3A(B), ._3B(B),
    ._3Y(nor7402_1__3y), ._4A(D), ._4B(D), ._4Y(nor7402_1__4y));
  NOR7402 nor7402_2 (
    ._1A(nor7402_1__2y), ._1B(nor7402_1__1y), ._1Y(nor7402_2__1y), ._2A(nor7402_2__1y), ._2B(A),
    ._2Y(nor7402_2__2y), ._3A(nor7402_1__3y), ._3B(nor7402_1__4y), ._3Y(nor7402_2__3y), ._4A(nor7402_2__2y),
    ._4B(nor7402_2__2y), ._4Y(nor7402_2__4y));
  NOR7402 nor7402_3 (._1A(D_3), ._1B(C_3), ._1Y(Y));  // open: _2A, _2B, _2Y, _3A, _3B, _3Y, _4A, _4B, _4Y
  NOR7402 nor7402_4 (
    ._1A(nor7402_2__3y), ._1B(nor7402_2__4y), ._1Y(nor7402_4__1y), ._2A(nor7402_4__1y), ._2B(nor7402_4__1y),
    ._2Y(W));  // open: _3A, _3B, _3Y, _4A, _4B, _4Y
  NOR7402 nor7402_5 (
    ._1A(D_2), ._1B(C_2), ._1Y(nor7402_5__1y), ._2A(nor7402_5__1y), ._2B(nor7402_5__1y), ._2Y(nor7402_5__2y),
    ._3A(B_2), ._3B(B_2), ._3Y(nor7402_5__3y), ._4A(nor7402_5__3y), ._4B(nor7402_5__2y), ._4Y(nor7402_5__4y));
  NOR7402 nor7402_6 (._1A(D_4), ._1B(D_4), ._1Y(Z));  // open: _2A, _2B, _2Y, _3A, _3B, _3Y, _4A, _4B, _4Y
  NOR7402 nor7402_7 (
    ._1A(D_2), ._1B(D_2), ._1Y(nor7402_7__1y), ._2A(nor7402_7__1y), ._2B(B_2), ._2Y(nor7402_7__2y),
    ._3A(C_2), ._3B(C_2), ._3Y(nor7402_7__3y), ._4A(nor7402_7__3y), ._4B(B_2), ._4Y(nor7402_7__4y));
  NOR7402 nor7402_8 (
    ._1A(nor7402_7__2y), ._1B(nor7402_5__4y), ._1Y(nor7402_8__1y), ._2A(nor7402_8__1y), ._2B(nor7402_8__1y),
    ._2Y(nor7402_8__2y), ._3A(nor7402_7__4y), ._3B(nor7402_8__2y), ._3Y(nor7402_8__3y), ._4A(nor7402_8__3y),
    ._4B(nor7402_8__3y), ._4Y(X));

  // Notes on the sheet:
  //   BC
  //   A
  //   A+BC+BD
  //   BD
  //   A+BC
  //   C'D'+CD
  //   B'
  //   C'D'B
  //   D'
  //   D'
  //   C'
  //   B'D
  //   B'C
  //   C'D'B+B'D
  //   C'D'B+B'D+B'C
endmodule
