// Logisim project Task_1.circ as structural Verilog: 1 circuit, main circuit main
module main (
  input  in_1,
  input  in_2,
  input  in_3,
  input  in_4,
  input  in_5,
  input  in_6,
  input  A_prime,
  input  in_8,
  input  in_9,
  input  in_10,
  input  in_11
);

  wire and_1_out, and_2_out, and_3_out, and_4_out, not_1_out, not_2_out, not_3_out, not_4_out, or_1_out,
       or_2_out, or_3_out;

  and and_1 (and_1_out, in_1, in_3);
  or or_1 (or_1_out, in_5, in_6);
  and and_2 (and_2_out, in_9, in_11);
  not not_1 (not_1_out, and_2_out);
  and and_3 (and_3_out, in_2, in_4);
  not not_2 (not_2_out, and_3_out);
  or or_2 (or_2_out, in_2, in_4);
  or or_3 (or_3_out, in_8, in_10);
  not not_3 (not_3_out, or_3_out);
  and and_4 (and_4_out, not_2_out, or_2_out);
  not not_4 (not_4_out, A_prime);

  // Notes on the sheet:
  //   AB
  //   A+B
  //   (A.B)'
  //   (A+B)'
  //   A^B
endmodule
