// Logisim project Task_2.circ as structural Verilog: 1 circuit, main circuit main
module main (
  input  A,
  input  A_2,
  input  B,
  input  B_2,
  input  C,
  input  C_2
);

  wire and_1_out, and_2_out, or_1_out, or_2_out;

  and and_1 (and_1_out, A, B);
  and and_2 (and_2_out, and_1_out, C);
  or or_1 (or_1_out, A_2, B_2);
  or or_2 (or_2_out, or_1_out, C_2);

  // Notes on the sheet:
  //   ABC
  //   A+B+C
endmodule
