// Logisim project Task_3.circ as structural Verilog: 1 circuit, main circuit main
module main (
  input  A,
  input  B,
  input  C,
  input  A_B__prime,
  input  in_5,
  input  in_6
);

  wire and_1_out, and_2_out, and_3_out, not_1_out, not_2_out, not_3_out, not_4_out, not_5_out, not_6_out,
       or_1_out, or_2_out, or_3_out;

  or or_1 (or_1_out, A_B__prime, in_5);
  and and_1 (and_1_out, A, B);
  not not_1 (not_1_out, and_1_out);
  not not_2 (not_2_out, or_1_out);
  and and_2 (and_2_out, not_1_out, not_1_out);
  not not_3 (not_3_out, and_2_out);
  or or_2 (or_2_out, not_2_out, not_2_out);
  not not_4 (not_4_out, or_2_out);
  and and_3 (and_3_out, not_3_out, C);
  not not_5 (not_5_out, and_3_out);
  or or_3 (or_3_out, not_4_out, in_6);
  not not_6 (not_6_out, or_3_out);

  // Notes on the sheet:
  //   (AB)'
  //   ((AB))'
  //   ((A+B))'
  //   (((AB))'C)'
  //   (((A+B))'+C)'
  //   (ABC)'
  //   (A+B+C)'
  //   3 input NAND from 2 input NAND
  //   3 input NOR from 2 input NOR
endmodule
