// Logisim project Task_1_1.circ as structural Verilog: 1 circuit, main circuit main
module main (
  input  A,
  input  B,
  input  C
);

  wire and_1_out, and_2_out, and_3_out, and_4_out, not_1_out, not_2_out, not_3_out, or_1_out, or_2_out,
       or_3_out, or_4_out, or_5_out, or_6_out, or_7_out, or_8_out, or_9_out, or_10_out;

  not not_1 (not_1_out, A);
  not not_2 (not_2_out, B);
  not not_3 (not_3_out, C);
  or or_1 (or_1_out, B, C);
  or or_2 (or_2_out, not_2_out, not_3_out);
  or or_3 (or_3_out, B, C);
  or or_4 (or_4_out, B, not_3_out);
  or or_5 (or_5_out, not_2_out, not_3_out);
  or or_6 (or_6_out, A, or_1_out);
  or or_7 (or_7_out, A, or_2_out);
  or or_8 (or_8_out, not_1_out, or_3_out);
  or or_9 (or_9_out, not_1_out, or_4_out);
  or or_10 (or_10_out, not_1_out, or_5_out);
  and and_1 (and_1_out, or_6_out, or_7_out);
  and and_2 (and_2_out, and_1_out, or_8_out);
  and and_3 (and_3_out, or_9_out, or_10_out);
  and and_4 (and_4_out, and_2_out, and_3_out);

  // Notes on the sheet:
  //   A+B+C
  //   A+B'+C'
  //   A'+B+C
  //   A'+B+C'
  //   A'+B'+C'
  //   (A+B+C)(A+B'+C')(A'+B+C)(A'+B+C')(A'+B'+C')
endmodule
