// Logisim project Task_2.circ as structural Verilog: 1 circuit, main circuit main
module main (
  input  A,
  input  B,
  input  C
);

  wire nand_1_out, nand_2_out, nand_3_out, nand_4_out, nand_5_out, nand_6_out, nand_7_out, nand_8_out;

  nand nand_1 (nand_1_out, C, C);
  nand nand_2 (nand_2_out, A, C);
  nand nand_3 (nand_3_out, B, nand_1_out);
  nand nand_4 (nand_4_out, nand_2_out, nand_2_out);
  nand nand_5 (nand_5_out, nand_3_out, nand_3_out);
  nand nand_6 (nand_6_out, nand_4_out, nand_4_out);
  nand nand_7 (nand_7_out, nand_5_out, nand_5_out);
  nand nand_8 (nand_8_out, nand_6_out, nand_7_out);

  // Notes on the sheet:
  //   C'
  //   (AC)'=(A'+C')
  //   (BC')'=(B'+C'')
  //   (B'+C'')'=B''.C'
  //   (A'+C')'=A''.C''
  //   (AC)'
  //   (BC')'
  //   AC+BC'
endmodule
