// Logisim project NAND_to_XNOR.circ as structural Verilog: 1 circuit, main circuit main
module main (
  input  A,
  input  B,
  output NAND
);

  wire and_1_out, and_2_out, and_3_out, and_4_out, and_5_out, not_1_out, not_2_out, not_3_out, not_4_out;

  and and_1 (and_1_out, A, A);
  and and_2 (and_2_out, B, B);
  not not_1 (not_1_out, and_1_out);
  not not_2 (not_2_out, and_2_out);
  and and_3 (and_3_out, A, B);
  not not_3 (not_3_out, and_3_out);
  and and_4 (and_4_out, not_1_out, not_2_out);
  not not_4 (not_4_out, and_4_out);
  and and_5 (and_5_out, not_3_out, not_4_out);
  not not_5 (NAND, and_5_out);

  // Notes on the sheet:
  //   NAND
  //   NAND
  //   NAND
  //   NAND
endmodule
