// Logisim project 2-bit_adder-subtractor.circ as structural Verilog
module main (
  input  A2,
  input  A1,
  input  B2,
  input  B1,
  input  M,
  output out_6,
  output out_7
);

  wire adder_1_cout, adder_2_cout, xor_1_out, xor_2_out;

  xor xor_1 (xor_1_out, B1, M);
  xor xor_2 (xor_2_out, B2, M);
  Adder #(.width(1)) adder_1 (.a(A1), .b(xor_1_out), .out(out_6), .cin(M), .cout(adder_1_cout));
  Adder #(.width(1)) adder_2 (.a(A2), .b(xor_2_out), .out(out_7), .cin(adder_1_cout), .cout(adder_2_cout));
endmodule
