// Logisim project 4-bit_adder_subtractor.circ as structural Verilog: 3 circuits, main circuit main
module main (
  input  M,
  input  A4,
  input  A3,
  input  A2,
  input  A1,
  input  B4,
  input  B3,
  input  B2,
  input  B1,
  output C4,
  output S4,
  output S3,
  output S2,
  output S1
);

  wire ic_7486_1__1y, ic_7486_1__2y, ic_7486_1__3y, ic_7486_1__4y;

  IC_7486 ic_7486_1 (
    ._1A(B4), ._1B(M), ._1Y(ic_7486_1__1y), ._2A(B3), ._2B(M), ._2Y(ic_7486_1__2y), ._3A(B2), ._3B(M),
    ._3Y(ic_7486_1__3y), ._4A(B1), ._4B(M), ._4Y(ic_7486_1__4y));
  IC7483_4_bit_adder ic7483_4_bit_adder_1 (
    .S1(S1), .S2(S2), .S3(S3), .S4(S4), .C4(C4), .A4(A4), .A3(A3), .A2(A2), .A1(A1), .B4(ic_7486_1__1y),
    .B3(ic_7486_1__2y), .B2(ic_7486_1__3y), .B1(ic_7486_1__4y), .M(M));
endmodule

// IC 7483
module IC7483_4_bit_adder (
  input  A4,
  input  A3,
  input  A2,
  input  A1,
  input  B4,
  input  B3,
  input  B2,
  input  B1,
  input  M,
  output S1,
  output S2,
  output S3,
  output S4,
  output C4
);

  wire adder_1_cout, adder_2_cout, adder_3_cout;

  Adder #(.width(1)) adder_1 (.a(A1), .b(B1), .out(S1), .cin(M), .cout(adder_1_cout));
  Adder #(.width(1)) adder_2 (.a(A2), .b(B2), .out(S2), .cin(adder_1_cout), .cout(adder_2_cout));
  Adder #(.width(1)) adder_3 (.a(A3), .b(B3), .out(S3), .cin(adder_2_cout), .cout(adder_3_cout));
  Adder #(.width(1)) adder_4 (.a(A4), .b(B4), .out(S4), .cin(adder_3_cout), .cout(C4));
endmodule

// XOR
module IC_7486 (
  input  _1A,
  input  _3A,
  input  _1B,
  input  _3B,
  input  _2A,
  input  _4A,
  input  _2B,
  input  _4B,
  output _1Y,
  output _3Y,
  output _2Y,
  output _4Y
);

  xor xor_1 (_1Y, _1A, _1B);
  xor xor_2 (_2Y, _2A, _2B);
  xor xor_3 (_3Y, _3A, _3B);
  xor xor_4 (_4Y, _4A, _4B);
endmodule
