// Logisim project 4-bit_binary_SUM_BCD.circ as structural Verilog: 5 circuits, main circuit main
module main (
  input  A4,
  input  A3,
  input  A2,
  input  A1,
  input  B4,
  input  B3,
  input  B2,
  input  B1,
  input  Cin,
  output S4,
  output S3,
  output S2,
  output S1,
  output Overflow
);

  wire ic7483_4_bit_adder_1_c4, ic7483_4_bit_adder_1_s1, ic7483_4_bit_adder_1_s2, ic7483_4_bit_adder_1_s3,
       ic7483_4_bit_adder_1_s4, ic_7408_1__1y, ic_7408_1__2y, ic_7432_1_or_9, ic_7432_1_or_11;

  IC7483_4_bit_adder ic7483_4_bit_adder_1 (
    .S1(ic7483_4_bit_adder_1_s1), .S2(ic7483_4_bit_adder_1_s2), .S3(ic7483_4_bit_adder_1_s3),
    .S4(ic7483_4_bit_adder_1_s4), .C4(ic7483_4_bit_adder_1_c4), .A4(A4), .A3(A3), .A2(A2), .A1(A1), .B4(B4),
    .B3(B3), .B2(B2), .B1(B1), .M(Cin));
  IC_7408 ic_7408_1 (
    ._1A(ic7483_4_bit_adder_1_s2), ._1B(ic7483_4_bit_adder_1_s4), ._1Y(ic_7408_1__1y),
    ._2A(ic7483_4_bit_adder_1_s3), ._2B(ic7483_4_bit_adder_1_s4), ._2Y(ic_7408_1__2y));  // open: _3A, _3B, _3Y, _4A, _4B, Y4
  IC7483_4_bit_adder ic7483_4_bit_adder_2 (
    .S1(S1), .S2(S2), .S3(S3), .S4(S4), .C4(Overflow), .A4(ic7483_4_bit_adder_1_s4),
    .A3(ic7483_4_bit_adder_1_s3), .A2(ic7483_4_bit_adder_1_s2), .A1(ic7483_4_bit_adder_1_s1), .B4(Cin),
    .B3(ic_7432_1_or_11), .B2(ic_7432_1_or_11), .B1(Cin), .M(Cin));
  IC_7432 ic_7432_1 (
    .OR(ic_7408_1__1y), .OR_3(ic_7408_1__2y), .OR_9(ic_7432_1_or_9), .OR_5(ic_7432_1_or_9),
    .OR_7(ic7483_4_bit_adder_1_c4), .OR_11(ic_7432_1_or_11));  // open: OR_2, OR_4, OR_10, OR_6, OR_8, OR_12
endmodule

// IC 7483
module IC7483_4_bit_adder (
  input  A4,
  input  A3,
  input  A2,
  input  A1,
  input  B4,
  input  B3,
  input  B2,
  input  B1,
  input  M,
  output S1,
  output S2,
  output S3,
  output S4,
  output C4
);

  wire adder_1_cout, adder_2_cout, adder_3_cout;

  Adder #(.width(1)) adder_1 (.a(A1), .b(B1), .out(S1), .cin(M), .cout(adder_1_cout));
  Adder #(.width(1)) adder_2 (.a(A2), .b(B2), .out(S2), .cin(adder_1_cout), .cout(adder_2_cout));
  Adder #(.width(1)) adder_3 (.a(A3), .b(B3), .out(S3), .cin(adder_2_cout), .cout(adder_3_cout));
  Adder #(.width(1)) adder_4 (.a(A4), .b(B4), .out(S4), .cin(adder_3_cout), .cout(C4));
endmodule

// XOR
module IC_7486 (
  input  _1A,
  input  _3A,
  input  _1B,
  input  _3B,
  input  _2A,
  input  _4A,
  input  _2B,
  input  _4B,
  output _1Y,
  output _3Y,
  output _2Y,
  output _4Y
);

  xor xor_1 (_1Y, _1A, _1B);
  xor xor_2 (_2Y, _2A, _2B);
  xor xor_3 (_3Y, _3A, _3B);
  xor xor_4 (_4Y, _4A, _4B);
endmodule

// AND
module IC_7408 (
  input  _1A,
  input  _3A,
  input  _1B,
  input  _3B,
  input  _2A,
  input  _4A,
  input  _2B,
  input  _4B,
  output _1Y,
  output _3Y,
  output _2Y,
  output Y4
);

  and and_1 (_1Y, _1A, _1B);
  and and_2 (_2Y, _2A, _2B);
  and and_3 (_3Y, _3A, _3B);
  and and_4 (Y4, _4A, _4B);
endmodule

// OR
module IC_7432 (
  input  OR,
  input  OR_2,
  input  OR_3,
  input  OR_4,
  input  OR_5,
  input  OR_6,
  input  OR_7,
  input  OR_8,
  output OR_9,
  output OR_10,
  output OR_11,
  output OR_12
);

  or u_OR (OR_9, OR, OR_3);
  or u_OR_2 (OR_11, OR_5, OR_7);
  or u_OR_3 (OR_10, OR_2, OR_4);
  or u_OR_4 (OR_12, OR_6, OR_8);
endmodule
