// Logisim project 8-bit_adder.circ as structural Verilog: 3 circuits, main circuit main
module main (
  input  A8,
  input  A7,
  input  A6,
  input  A5,
  input  A4,
  input  A3,
  input  A2,
  input  A1,
  input  B8,
  input  B7,
  input  B6,
  input  B5,
  input  B4,
  input  B3,
  input  B2,
  input  B1,
  input  Cin,
  output S1,
  output S2,
  output S3,
  output S4,
  output S5,
  output S6,
  output S7,
  output S8,
  output OverFlow
);

  wire ic7483_4_bit_adder_1_c4;

  IC7483_4_bit_adder ic7483_4_bit_adder_1 (
    .S1(S1), .S2(S2), .S3(S3), .S4(S4), .C4(ic7483_4_bit_adder_1_c4), .A4(A4), .A3(A3), .A2(A2), .A1(A1),
    .B4(B4), .B3(B3), .B2(B2), .B1(B1), .M(Cin));
  IC7483_4_bit_adder ic7483_4_bit_adder_2 (
    .S1(S5), .S2(S6), .S3(S7), .S4(S8), .C4(OverFlow), .A4(A8), .A3(A7), .A2(A6), .A1(A5), .B4(B8), .B3(B7),
    .B2(B6), .B1(B5), .M(ic7483_4_bit_adder_1_c4));
endmodule

// IC 7483
module IC7483_4_bit_adder (
  input  A4,
  input  A3,
  input  A2,
  input  A1,
  input  B4,
  input  B3,
  input  B2,
  input  B1,
  input  M,
  output S1,
  output S2,
  output S3,
  output S4,
  output C4
);

  wire adder_1_cout, adder_2_cout, adder_3_cout;

  Adder #(.width(1)) adder_1 (.a(A1), .b(B1), .out(S1), .cin(M), .cout(adder_1_cout));
  Adder #(.width(1)) adder_2 (.a(A2), .b(B2), .out(S2), .cin(adder_1_cout), .cout(adder_2_cout));
  Adder #(.width(1)) adder_3 (.a(A3), .b(B3), .out(S3), .cin(adder_2_cout), .cout(adder_3_cout));
  Adder #(.width(1)) adder_4 (.a(A4), .b(B4), .out(S4), .cin(adder_3_cout), .cout(C4));
endmodule

// XOR
module IC_7486 (
  input  _1A,
  input  _3A,
  input  _1B,
  input  _3B,
  input  _2A,
  input  _4A,
  input  _2B,
  input  _4B,
  output _1Y,
  output _3Y,
  output _2Y,
  output _4Y
);

  xor xor_1 (_1Y, _1A, _1B);
  xor xor_2 (_2Y, _2A, _2B);
  xor xor_3 (_3Y, _3A, _3B);
  xor xor_4 (_4Y, _4A, _4B);
endmodule
