// Logisim project BCD_seven_segment_decoder.circ as structural Verilog: 7 circuits, main circuit main
// 7408 AND
module AND7408 (
  input  _1A,
  input  _3A,
  input  _1B,
  input  _3B,
  input  _2A,
  input  _4A,
  input  _2B,
  input  _4B,
  output _1Y,
  output _3Y,
  output _2Y,
  output Y4
);

  and and_1 (_1Y, _1A, _1B);
  and and_2 (_2Y, _2A, _2B);
  and and_3 (_3Y, _3A, _3B);
  and and_4 (Y4, _4A, _4B);
endmodule

module NAND7400 (
  input  _1A,
  input  _3A,
  input  _1B,
  input  _3B,
  input  _2A,
  input  _4A,
  input  _2B,
  input  _4B,
  output _1Y,
  output _3Y,
  output _2Y,
  output _4Y
);

  wire and_1_out, and_2_out, and_3_out, and_4_out;

  and and_1 (and_1_out, _1A, _1B);
  and and_2 (and_2_out, _2A, _2B);
  not not_1 (_1Y, and_1_out);
  not not_2 (_3Y, and_3_out);
  not not_3 (_4Y, and_4_out);
  not not_4 (_2Y, and_2_out);
  and and_3 (and_3_out, _3A, _3B);
  and and_4 (and_4_out, _4A, _4B);
endmodule

// 7432 OR
module OR7432 (
  input  _1A,
  input  _3A,
  input  _1B,
  input  _3B,
  input  _2A,
  input  _4A,
  input  _2B,
  input  _4B,
  output _1Y,
  output _3Y,
  output _2Y,
  output _4Y
);

  or or_1 (_1Y, _1A, _1B);
  or or_2 (_2Y, _2A, _2B);
  or or_3 (_3Y, _3A, _3B);
  or or_4 (_4Y, _4A, _4B);
endmodule

// 7404 NOT
module NOT7404 (
  input  _1A,
  input  _4A,
  input  _2A,
  input  _5A,
  input  _3A,
  input  _6A,
  output _1Y,
  output _4Y,
  output _2Y,
  output _5Y,
  output _3Y,
  output _6Y
);

  not not_1 (_1Y, _1A);
  not not_2 (_2Y, _2A);
  not not_3 (_3Y, _3A);
  not not_4 (_4Y, _4A);
  not not_5 (_5Y, _5A);
  not not_6 (_6Y, _6A);
endmodule

module XOR7486 (
  input  _1A,
  input  _3A,
  input  _1B,
  input  _3B,
  input  _2A,
  input  _4A,
  input  _2B,
  input  _4B,
  output _1Y,
  output _3Y,
  output _2Y,
  output _4Y
);

  xor xor_1 (_1Y, _1A, _1B);
  xor xor_2 (_2Y, _2A, _2B);
  xor xor_3 (_3Y, _3A, _3B);
  xor xor_4 (_4Y, _4A, _4B);
endmodule

// 7402 NOR
module NOR7402 (
  input  _1A,
  input  _3A,
  input  _1B,
  input  _3B,
  input  _2A,
  input  _4A,
  input  _2B,
  input  _4B,
  output _1Y,
  output _3Y,
  output _2Y,
  output _4Y
);

  wire or_1_out, or_2_out, or_3_out, or_4_out;

  or or_1 (or_1_out, _1A, _1B);
  or or_2 (or_2_out, _2A, _2B);
  not not_1 (_3Y, or_3_out);
  not not_2 (_1Y, or_1_out);
  not not_3 (_4Y, or_4_out);
  not not_4 (_2Y, or_2_out);
  or or_3 (or_3_out, _3A, _3B);
  or or_4 (or_4_out, _4A, _4B);
endmodule

module main (
  input  D,
  input  C,
  input  B,
  input  A
);

  wire and7408_1__1y, and7408_1__2y, and7408_2__1y, and7408_2__2y, and7408_3__1y, and7408_3__2y,
       and7408_4__1y, and7408_4__2y, and7408_4_y4, and7408_5__1y, and7408_5__2y, and7408_6__1y,
       and7408_6__2y, and7408_6__3y, and7408_7__1y, and7408_7__2y, and7408_7__3y, not7404_1__4y,
       not7404_2__4y, not7404_3__4y, not7404_4__4y, or7432_1__1y, or7432_1__2y, or7432_2__1y, or7432_2__2y,
       or7432_2__4y, or7432_3__1y, or7432_3__2y, or7432_4__1y, or7432_4__2y, or7432_4__3y, or7432_4__4y,
       or7432_5__1y, or7432_6__1y, or7432_6__2y, or7432_6__3y, or7432_7__1y, or7432_7__2y, or7432_7__3y;

  NOT7404 not7404_1 (._4A(D), ._4Y(not7404_1__4y));  // open: _1A, _1Y, _2A, _2Y, _3A, _3Y, _5A, _5Y, _6A, _6Y
  NOT7404 not7404_2 (._4A(C), ._4Y(not7404_2__4y));  // open: _1A, _1Y, _2A, _2Y, _3A, _3Y, _5A, _5Y, _6A, _6Y
  NOT7404 not7404_3 (._4A(B), ._4Y(not7404_3__4y));  // open: _1A, _1Y, _2A, _2Y, _3A, _3Y, _5A, _5Y, _6A, _6Y
  NOT7404 not7404_4 (._4A(A), ._4Y(not7404_4__4y));  // open: _1A, _1Y, _2A, _2Y, _3A, _3Y, _5A, _5Y, _6A, _6Y
  AND7408 and7408_1 (
    ._1A(C), ._1B(A), ._1Y(and7408_1__1y), ._2A(not7404_2__4y), ._2B(not7404_4__4y), ._2Y(and7408_1__2y));  // open: _3A, _3B, _3Y, _4A, _4B, Y4
  AND7408 and7408_2 (
    ._1A(not7404_3__4y), ._1B(not7404_4__4y), ._1Y(and7408_2__1y), ._2A(B), ._2B(A), ._2Y(and7408_2__2y));  // open: _3A, _3B, _3Y, _4A, _4B, Y4
  OR7432 or7432_1 (
    ._1A(C), ._1B(not7404_3__4y), ._1Y(or7432_1__1y), ._2A(or7432_1__1y), ._2B(A), ._2Y(or7432_1__2y));  // open: _3A, _3B, _3Y, _4A, _4B, _4Y
  AND7408 and7408_3 (
    ._1A(not7404_2__4y), ._1B(not7404_4__4y), ._1Y(and7408_3__1y), ._2A(not7404_4__4y), ._2B(B),
    ._2Y(and7408_3__2y));  // open: _3A, _3B, _3Y, _4A, _4B, Y4
  AND7408 and7408_4 (
    ._1A(C), ._1B(not7404_3__4y), ._1Y(and7408_4__1y), ._2A(and7408_4__1y), ._2B(A), ._2Y(and7408_4__2y),
    ._4A(not7404_2__4y), ._4B(B), .Y4(and7408_4_y4));  // open: _3A, _3B, _3Y
  AND7408 and7408_5 (
    ._1A(not7404_2__4y), ._1B(not7404_4__4y), ._1Y(and7408_5__1y), ._2A(not7404_4__4y), ._2B(B),
    ._2Y(and7408_5__2y));  // open: _3A, _3B, _3Y, _4A, _4B, Y4
  AND7408 and7408_6 (
    ._1A(C), ._1B(not7404_3__4y), ._1Y(and7408_6__1y), ._2A(not7404_4__4y), ._2B(C), ._2Y(and7408_6__2y),
    ._3A(not7404_3__4y), ._3B(not7404_4__4y), ._3Y(and7408_6__3y));  // open: _4A, _4B, Y4
  AND7408 and7408_7 (
    ._1A(not7404_3__4y), ._1B(C), ._1Y(and7408_7__1y), ._2A(B), ._2B(not7404_4__4y), ._2Y(and7408_7__2y),
    ._3A(B), ._3B(not7404_2__4y), ._3Y(and7408_7__3y));  // open: _4A, _4B, Y4
  OR7432 or7432_2 (
    ._1A(B), ._1B(D), ._1Y(or7432_2__1y), ._2A(or7432_2__1y), ._2B(and7408_1__1y), ._2Y(or7432_2__2y),
    ._4A(and7408_1__2y), ._4B(or7432_2__2y), ._4Y(or7432_2__4y));  // open: _3A, _3B, _3Y
  OR7432 or7432_3 (
    ._1A(and7408_2__1y), ._1B(and7408_2__2y), ._1Y(or7432_3__1y), ._2A(or7432_3__1y), ._2B(not7404_2__4y),
    ._2Y(or7432_3__2y));  // open: _3A, _3B, _3Y, _4A, _4B, _4Y
  OR7432 or7432_4 (
    ._1A(D), ._1B(and7408_3__1y), ._1Y(or7432_4__1y), ._2A(or7432_4__1y), ._2B(and7408_3__2y),
    ._2Y(or7432_4__2y), ._3A(or7432_4__2y), ._3B(and7408_4__2y), ._3Y(or7432_4__3y), ._4A(or7432_4__3y),
    ._4B(and7408_4_y4), ._4Y(or7432_4__4y));
  OR7432 or7432_5 (
    ._1A(and7408_5__1y), ._1B(and7408_5__2y), ._1Y(or7432_5__1y));  // open: _2A, _2B, _2Y, _3A, _3B, _3Y, _4A, _4B, _4Y
  OR7432 or7432_6 (
    ._1A(and7408_6__1y), ._1B(and7408_6__2y), ._1Y(or7432_6__1y), ._2A(or7432_6__1y), ._2B(D),
    ._2Y(or7432_6__2y), ._3A(or7432_6__2y), ._3B(and7408_6__3y), ._3Y(or7432_6__3y));  // open: _4A, _4B, _4Y
  OR7432 or7432_7 (
    ._1A(and7408_7__1y), ._1B(and7408_7__2y), ._1Y(or7432_7__1y), ._2A(or7432_7__1y), ._2B(D),
    ._2Y(or7432_7__2y), ._3A(and7408_7__3y), ._3B(or7432_7__2y), ._3Y(or7432_7__3y));  // open: _4A, _4B, _4Y
  _7_Segment_Display u_7_segment_display_1 (
    .g(or7432_7__3y), .f(or7432_6__3y), .a(or7432_2__4y), .b(or7432_3__2y), .e(or7432_5__1y),
    .d(or7432_4__4y), .c(or7432_1__2y));  // open: dp
endmodule
