// Logisim project Flip Flop.circ as structural Verilog: 4 circuits, main circuit Jk-Flip-Flop
module Jk_Flip_Flop (
  input  K,
  input  J,
  output Q,
  output Q_prime
);

  wire and_1_out, and_2_out, CLK_out;

  Clock CLK (.out(CLK_out));
  and and_1 (and_1_out, Q, K, CLK_out);
  and and_2 (and_2_out, CLK_out, J, Q_prime);
  nor nor_1 (Q, and_1_out, Q_prime);
  nor nor_2 (Q_prime, Q, and_2_out);
endmodule

module TFlipFlop (
  input  in_1
);

  wire clock_1_out, j_k_ff_1_q;

  Clock clock_1 (.out(clock_1_out));
  J_K_Flip_Flop j_k_ff_1 (.J(in_1), .clk(clock_1_out), .K(in_1), .Q(j_k_ff_1_q));  // open: Qn, preset, en, reset
endmodule

module DflipFlop (
  input  in_1
);

  wire clock_1_out, j_k_ff_1_q, not_1_out;

  Clock clock_1 (.out(clock_1_out));
  J_K_Flip_Flop j_k_ff_1 (.J(in_1), .clk(clock_1_out), .K(not_1_out), .Q(j_k_ff_1_q));  // open: Qn, preset, en, reset
  not not_1 (not_1_out, in_1);
endmodule

module Register (
  input  in_1,
  input  in_2
);

  wire clock_1_out, clock_2_out, d_ff_1_q, d_ff_2_q, d_ff_3_q, d_ff_4_q, d_ff_5_q, d_ff_6_q, d_ff_7_q,
       d_ff_8_q;

  Clock clock_1 (.out(clock_1_out));
  D_Flip_Flop d_ff_1 (.clk(clock_2_out), .D(in_2), .Q(d_ff_1_q));  // open: Qn, preset, en, reset
  LED led_1 (.in(d_ff_2_q));
  D_Flip_Flop d_ff_2 (.clk(clock_1_out), .D(in_1), .Q(d_ff_2_q));  // open: Qn, preset, en, reset
  LED led_2 (.in(d_ff_1_q));
  D_Flip_Flop d_ff_3 (.clk(clock_2_out), .D(d_ff_1_q), .Q(d_ff_3_q));  // open: Qn, preset, en, reset
  LED led_3 (.in(d_ff_5_q));
  D_Flip_Flop d_ff_4 (.clk(clock_1_out), .D(d_ff_5_q), .Q(d_ff_4_q));  // open: Qn, preset, en, reset
  D_Flip_Flop d_ff_5 (.clk(clock_1_out), .D(d_ff_2_q), .Q(d_ff_5_q));  // open: Qn, preset, en, reset
  LED led_4 (.in(d_ff_3_q));
  D_Flip_Flop d_ff_6 (.clk(clock_2_out), .D(d_ff_3_q), .Q(d_ff_6_q));  // open: Qn, preset, en, reset
  LED led_5 (.in(d_ff_4_q));
  LED led_6 (.in(d_ff_7_q));
  D_Flip_Flop d_ff_7 (.clk(clock_1_out), .D(d_ff_4_q), .Q(d_ff_7_q));  // open: Qn, preset, en, reset
  LED led_7 (.in(d_ff_6_q));
  D_Flip_Flop d_ff_8 (.clk(clock_2_out), .D(d_ff_6_q), .Q(d_ff_8_q));  // open: Qn, preset, en, reset
  Clock clock_2 (.out(clock_2_out));
  LED led_8 (.in(d_ff_8_q));
endmodule
