// Logisim project MUX.circ as structural Verilog: 3 circuits, main circuit main
module main (
  input  C,
  input  _1,
  input  _0,
  input  S0,
  input  S1,
  input  C_2,
  input  _1_2,
  input  _0_2,
  input  S0_2,
  input  S1_2,
  input  S2,
  output F
);

  wire not_1_out, not_2_out;

  not not_1 (not_1_out, C);
  _4_1_MUX u_4_1_mux_1 (.in_1(not_1_out), .in_2(_1), .in_3(_0), .in_4(C), .out_7(F), .in_5(S0), .in_6(S1));
  not not_2 (not_2_out, C_2);
  _8_1_MUX u_8_1_mux_1 (
    .I0(_1_2), .I1(_1_2), .I2(_0_2), .I3(not_2_out), .I4(_0_2), .I5(not_2_out), .I6(C_2), .I7(C_2),
    .in_9(S0_2), .in_10(S1_2), .in_11(S2));  // open: F

  // Notes on the sheet:
  //   F(A,B,C)=sum(0,1,5,7)
  //   F(A,B,C,D)=sum(0,1,3,5,8,9,14,15)
endmodule

module _4_1_MUX (
  input  in_1,
  input  in_2,
  input  in_3,
  input  in_4,
  input  in_5,
  input  in_6,
  output out_7
);

  wire and_1_out, and_2_out, and_3_out, and_4_out, not_1_out, not_2_out;

  not not_1 (not_1_out, in_5);
  not not_2 (not_2_out, in_6);
  and and_1 (and_1_out, in_1, not_1_out, not_2_out);
  and and_2 (and_2_out, in_2, not_1_out, in_6);
  and and_3 (and_3_out, in_3, in_5, not_2_out);
  and and_4 (and_4_out, in_4, in_5, in_6);
  or or_1 (out_7, and_1_out, and_2_out, and_3_out, and_4_out);
endmodule

module _8_1_MUX (
  input  I0,
  input  I1,
  input  I2,
  input  I3,
  input  I4,
  input  I5,
  input  I6,
  input  I7,
  input  in_9,
  input  in_10,
  input  in_11,
  output F
);

  wire and_1_out, and_2_out, and_3_out, and_4_out, and_5_out, and_6_out, and_7_out, and_8_out, not_1_out,
       not_2_out, not_3_out;

  not not_1 (not_1_out, in_9);
  not not_2 (not_2_out, in_10);
  not not_3 (not_3_out, in_11);
  and and_1 (and_1_out, I0, not_1_out, not_2_out, not_3_out);
  and and_2 (and_2_out, I1, not_1_out, not_2_out, in_11);
  and and_3 (and_3_out, I2, not_1_out, in_10, not_3_out);
  and and_4 (and_4_out, I3, not_1_out, in_10, in_11);
  and and_5 (and_5_out, I4, in_9, not_2_out, not_3_out);
  and and_6 (and_6_out, I5, in_9, not_2_out, in_11);
  and and_7 (and_7_out, I6, in_9, in_10, not_3_out);
  and and_8 (and_8_out, I7, in_9, in_10, in_11);
  or or_1 (F, and_1_out, and_2_out, and_3_out, and_4_out, and_5_out, and_6_out, and_7_out, and_8_out);
endmodule
